// Logisim project P01_01C.circ as structural Verilog: 1 circuit, main circuit main
module main (
  input  A,
  input  B,
  input  C,
  input  D,
  output S
);

  wire and_1_out, and_2_out, and_3_out, and_4_out, not_1_out, not_2_out, not_3_out, not_4_out, not_5_out,
       not_6_out;

  not not_1 (not_1_out, C);
  not not_2 (not_2_out, A);
  not not_3 (not_3_out, B);
  not not_4 (not_4_out, A);
  not not_5 (not_5_out, B);
  not not_6 (not_6_out, D);
  and and_1 (and_1_out, B, not_1_out, D);
  and and_2 (and_2_out, not_2_out, B, C, D);
  and and_3 (and_3_out, A, not_3_out, C, D);
  and and_4 (and_4_out, not_4_out, not_5_out, C, not_6_out);
  or or_1 (S, and_1_out, and_2_out, and_3_out, and_4_out);
endmodule
