// Logisim project P01_01D.circ as structural Verilog: 1 circuit, main circuit main
module main (
  input  A,
  input  B,
  input  C,
  input  D,
  output S
);

  wire not_1_out, not_2_out, not_3_out, not_4_out, not_5_out, not_6_out, not_7_out, not_8_out, not_9_out,
       or_1_out, or_2_out, or_3_out, or_4_out, or_5_out, or_6_out;

  or or_1 (or_1_out, B, C, D);
  or or_2 (or_2_out, C, not_1_out);
  not not_1 (not_1_out, D);
  or or_3 (or_3_out, A, B, not_2_out);
  not not_2 (not_2_out, D);
  not not_3 (not_3_out, A);
  not not_4 (not_4_out, B);
  or or_4 (or_4_out, not_3_out, not_4_out, not_5_out);
  not not_5 (not_5_out, C);
  not not_6 (not_6_out, B);
  not not_7 (not_7_out, C);
  or or_5 (or_5_out, not_6_out, not_7_out, D);
  not not_8 (not_8_out, A);
  or or_6 (or_6_out, not_8_out, not_9_out, D);
  not not_9 (not_9_out, C);
  and and_1 (S, or_1_out, or_2_out, or_3_out, or_4_out, or_5_out, or_6_out);
endmodule
