// Logisim project P01_01E.circ as structural Verilog: 1 circuit, main circuit main
module main (
  input  A,
  input  B,
  input  C,
  input  D,
  output S
);

  wire nand_1_out, nand_2_out, nand_3_out, nand_4_out, not_1_out, not_2_out, not_3_out, not_4_out, not_5_out,
       not_6_out, not_7_out;

  nand nand_1 (nand_1_out, B, not_1_out, not_2_out);
  not not_1 (not_1_out, C);
  not not_2 (not_2_out, D);
  not not_3 (not_3_out, A);
  nand nand_2 (nand_2_out, not_3_out, B, C, D);
  not not_4 (not_4_out, B);
  nand nand_3 (nand_3_out, A, not_4_out, C, D);
  not not_5 (not_5_out, A);
  not not_6 (not_6_out, B);
  nand nand_4 (nand_4_out, not_5_out, not_6_out, C, not_7_out);
  not not_7 (not_7_out, D);
  nand nand_5 (S, nand_1_out, nand_2_out, nand_3_out, nand_4_out);
endmodule
