// Logisim project P01_01F.circ as structural Verilog: 1 circuit, main circuit main
module main (
  input  A,
  input  B,
  input  C,
  input  D,
  output S
);

  wire nor_1_out, nor_2_out, nor_3_out, nor_4_out, nor_5_out, nor_6_out, not_1_out, not_2_out, not_3_out,
       not_4_out, not_5_out, not_6_out, not_7_out, not_8_out, not_9_out;

  nor nor_1 (nor_1_out, B, C, D);
  nor nor_2 (nor_2_out, C, not_1_out);
  not not_1 (not_1_out, D);
  nor nor_3 (nor_3_out, A, B, not_2_out);
  not not_2 (not_2_out, D);
  not not_3 (not_3_out, A);
  not not_4 (not_4_out, B);
  nor nor_4 (nor_4_out, not_3_out, not_4_out, not_5_out);
  not not_5 (not_5_out, C);
  not not_6 (not_6_out, B);
  not not_7 (not_7_out, C);
  nor nor_5 (nor_5_out, not_6_out, not_7_out, D);
  not not_8 (not_8_out, A);
  not not_9 (not_9_out, C);
  nor nor_6 (nor_6_out, not_8_out, not_9_out, D);
  nor nor_7 (S, nor_1_out, nor_2_out, nor_3_out, nor_4_out, nor_5_out, nor_6_out);
endmodule
