// Logisim project P01_02.circ as structural Verilog: 1 circuit, main circuit main
module main (
  input  X,
  input  Y,
  output S
);

  wire not_1_out, W1_out, W2_out, W3_out, W4_out;

  not W1 (W1_out, X);
  not W2 (W2_out, Y);
  and W3 (W3_out, W1_out, Y);
  or W4 (W4_out, W2_out, X);
  not not_1 (not_1_out, W4_out);
  and and_1 (S, W3_out, not_1_out);
endmodule
