// Logisim project P01_04.circ as structural Verilog: 1 circuit, main circuit main
module main (
  input  A,
  input  B,
  output S
);

  wire nor_1_out, not_1_out, not_2_out, xor_1_out;

  not not_1 (not_1_out, A);
  not not_2 (not_2_out, B);
  xor xor_1 (xor_1_out, A, B);
  nor nor_1 (nor_1_out, not_1_out, not_2_out);
  nand nand_1 (S, xor_1_out, nor_1_out);
endmodule
