// Logisim project Guia_0501.circ as structural Verilog: 1 circuit, main circuit main
module main (
  input  B,
  input  A,
  output S
);

  wire not_1_out, or_1_out, or_2_out;

  or or_1 (or_1_out, A, A);
  not not_1 (not_1_out, or_1_out);
  or or_2 (or_2_out, B, not_1_out);
  not not_2 (S, or_2_out);
endmodule
